# Fritzing sketch POC Wiring (saved by Fritzing 0.9.4)
breadboards: 1

parts:
  Composant1 = Arduino Uno (Rev3)
  LCD1 = LCD screen
  SG1 = Buzzer 12mm [package=buzzer-ccv-kit]
  R1 = Resistor [tolerance=±5% resistance=220 package="0402 [SMD]"]

nets:
  N1: Composant1.D8, SG1.2
  N2: Composant1.5V, R1.Pin_0
  N3: Composant1.GND, LCD1.DB0, LCD1.DB1, LCD1.DB2, LCD1.DB3, LCD1.LED-, SG1.1
  N4: LCD1.LED+, R1.Pin_1
